# Fritzing sketch LDR (saved by Fritzing 0.9.2b)
breadboards: 1

parts:
  C1 = Electrolytic Capacitor [capacitance=1µF package="100 mil [THT, electrolytic]"]
  R1 = Photocell (LDR) [package=THT]
  J1 = Piezo Speaker  # not connected
  SG1 = Buzzer 12mm [package=buzzer-ccv]  # not connected
  SG2 = Buzzer 12mm [package=buzzer-ccv-kit]  # not connected
  SG3 = Buzzer 12mm [package=buzzer-12mm]  # not connected
  J2 = Piezo Speaker  # not connected
  Raspberry_Pi1 = Raspberry Pi 2

nets:
  N1: C1.-, R1.pin_1, Raspberry_Pi1.GPIO4
  N2: C1.+, Raspberry_Pi1.GND
  N3: R1.pin_0, Raspberry_Pi1.3v3
