# Fritzing sketch LDR_true (saved by Fritzing 0.9.2b)
breadboards: 1

parts:
  C1 = Electrolytic Capacitor [capacitance=1µF package="100 mil [THT, electrolytic]"]
  R1 = Photocell (LDR) [package=THT]
  Raspberry_Pi1 = Raspberry Pi 2

nets:
  N1: C1.-, R1.pin_1, Raspberry_Pi1.GPIO4
  N2: C1.+, Raspberry_Pi1.GND
  N3: R1.pin_0, Raspberry_Pi1.3v3
